// Logisim project project_cleancirc.circ as structural Verilog: 6 circuits, main circuit main
module main (
);

  wire ALU_carry_out, alusrc, button_1_out, carry_in, CLK, clock_1_out, halt, j, jal, ld, li, memwe,
       pc_rd_we, put, reg_we, rs_we, st;
  wire [1:0] regsrc;
  wire [2:0] multiplexer_5_out, multiplexer_6_out, pc_op, rdidx, rsidx;
  wire [3:0] aluop, display_1_out_5, display_1_out_6, display_1_out_7, display_1_out_8;
  wire [7:0] imm, multiplexer_1_out, multiplexer_4_out, multiplexer_7_out, multiplexer_8_out,
       multiplexer_9_out, multiplexer_10_out, multiplexer_11_out, pc_out, ram_1_data, reg_rd,
       reg_rd_input_alu, reg_rd_input_imm, reg_rd_input_mem, reg_rd_input_pc, reg_rs;
  wire [15:0] instruction;

  // Probe on instruction
  // Probe on pc_out
  Multiplexer #(.width(8)) multiplexer_1 (.in1(reg_rd), .out(multiplexer_1_out), .sel(st));  // open: in0, en
  control control_1 (
    .Instruction(instruction), .imm(imm), .memwe(memwe), .rs(rsidx), .rd(rdidx), .reg_src(regsrc),
    .HALT(halt), .put(put), .li(li), .ld(ld), .st(st), .j(j), .jal(jal), .pc_we(pc_rd_we), .ALUOp(aluop),
    .PC_op(pc_op), .alu_src(alusrc), .rs_we(rs_we), .reg_we(reg_we));
  ROM #(.dataWidth(16)) rom_1 (.addr(pc_out), .data(instruction));  // open: sel
  RAM #(.bus("separate")) ram_1 (
    .addr(reg_rs), .din(multiplexer_1_out), .data(ram_1_data), .str(memwe), .clk(CLK));  // open: sel, ld, clr
  Multiplexer #(.width(8)) multiplexer_2 (.in1(ram_1_data), .out(reg_rd_input_mem), .sel(ld));  // open: in0, en
  Multiplexer #(.width(8)) multiplexer_3 (.in1(imm), .out(reg_rd_input_imm), .sel(li));  // open: in0, en
  Multiplexer #(.select(2), .width(8)) multiplexer_4 (
    .in0(reg_rd_input_alu), .in1(reg_rd_input_mem), .in2(reg_rd_input_imm), .in3(reg_rd_input_pc),
    .out(multiplexer_4_out), .sel(regsrc));  // open: en
  LED led_1 (.in(halt));
  Clock clock_1 (.out(clock_1_out));
  or or_1 (CLK, clock_1_out, button_1_out);
  Button button_1 (.out(button_1_out));
  Multiplexer #(.width(3)) multiplexer_5 (.in0(3'b000), .in1(rsidx), .out(multiplexer_5_out), .sel(rs_we));  // open: en
  Multiplexer #(.width(3)) multiplexer_6 (.in0(rdidx), .in1(3'b000), .out(multiplexer_6_out), .sel(j));  // open: en
  register register_1 (
    .data(multiplexer_4_out), .WE(reg_we), .rs(multiplexer_5_out), .rd(multiplexer_6_out), .in_5(CLK),
    .rd_out(reg_rd), .rs_out(reg_rs));
  Multiplexer #(.width(8)) multiplexer_7 (.in1(reg_rs), .out(multiplexer_7_out), .sel(put));  // open: in0, en
  Multiplexer #(.width(8)) multiplexer_8 (.in1(reg_rd), .out(multiplexer_8_out), .sel(put));  // open: in0, en
  Multiplexer #(.width(8)) multiplexer_9 (.in1(reg_rd), .out(multiplexer_9_out), .sel(pc_rd_we));  // open: in0, en
  Display display_1 (
    .in_1(CLK), .En(1'b1), .In(multiplexer_7_out), .In_2(multiplexer_8_out), .out_5(display_1_out_5),
    .out_6(display_1_out_6), .out_7(display_1_out_7), .out_8(display_1_out_8));
  Multiplexer #(.width(8)) multiplexer_10 (
    .in0(reg_rs), .in1(imm), .out(multiplexer_10_out), .sel(alusrc));  // open: en
  pc_control pc_control_1 (
    .pc_op(pc_op), .clk(CLK), .imm(imm), .halt(halt), .reg_rd(multiplexer_9_out), .pc_out(pc_out));
  Hex_Digit_Display hex_digit_display_1 (.value(display_1_out_5));  // open: dp
  Hex_Digit_Display hex_digit_display_2 (.value(display_1_out_6));  // open: dp
  ALU ALU (
    .Carry_In(carry_in), .A(reg_rd), .B(multiplexer_10_out), .Op(aluop), .Result(reg_rd_input_alu),
    .Carry_Out(ALU_carry_out));
  Multiplexer #(.width(8)) multiplexer_11 (.in1(pc_out), .out(multiplexer_11_out), .sel(jal));  // open: in0, en
  Adder adder_1 (.a(multiplexer_11_out), .b(8'h1), .out(reg_rd_input_pc));  // open: cin, cout
  Hex_Digit_Display hex_digit_display_3 (.value(display_1_out_7));  // open: dp
  Hex_Digit_Display hex_digit_display_4 (.value(display_1_out_8));  // open: dp
  Register #(.width(1)) register_2 (.D(ALU_carry_out), .en(1'b1), .Q(carry_in), .clk(CLK));  // open: clr

  // Notes on the sheet:
  //   contents of rom_1 (hex, n*v repeats v):
  //   b706 b703 0 119f 900 af00 1154 900 af00
endmodule

module Display (
  input  in_1,
  input  En,
  input  [7:0] In,
  input  [7:0] In_2,
  output [3:0] out_5,
  output [3:0] out_6,
  output [3:0] out_7,
  output [3:0] out_8
);

  D_Flip_Flop LSB (.clk(in_1), .D(In[0]), .Q(out_6[0]), .en(En));  // open: Qn, preset, reset
  D_Flip_Flop d_ff_1 (.clk(in_1), .D(In[1]), .Q(out_6[1]), .en(En));  // open: Qn, preset, reset
  D_Flip_Flop d_ff_2 (.clk(in_1), .D(In[2]), .Q(out_6[2]), .en(En));  // open: Qn, preset, reset
  D_Flip_Flop d_ff_3 (.clk(in_1), .D(In[3]), .Q(out_6[3]), .en(En));  // open: Qn, preset, reset
  D_Flip_Flop LSB_2 (.clk(in_1), .D(In[4]), .Q(out_5[0]), .en(En));  // open: Qn, preset, reset
  D_Flip_Flop d_ff_4 (.clk(in_1), .D(In[5]), .Q(out_5[1]), .en(En));  // open: Qn, preset, reset
  D_Flip_Flop d_ff_5 (.clk(in_1), .D(In[6]), .Q(out_5[2]), .en(En));  // open: Qn, preset, reset
  D_Flip_Flop d_ff_6 (.clk(in_1), .D(In[7]), .Q(out_5[3]), .en(En));  // open: Qn, preset, reset
  D_Flip_Flop LSB_3 (.clk(in_1), .D(In_2[0]), .Q(out_8[0]), .en(En));  // open: Qn, preset, reset
  D_Flip_Flop d_ff_7 (.clk(in_1), .D(In_2[1]), .Q(out_8[1]), .en(En));  // open: Qn, preset, reset
  D_Flip_Flop d_ff_8 (.clk(in_1), .D(In_2[2]), .Q(out_8[2]), .en(En));  // open: Qn, preset, reset
  D_Flip_Flop d_ff_9 (.clk(in_1), .D(In_2[3]), .Q(out_8[3]), .en(En));  // open: Qn, preset, reset
  D_Flip_Flop LSB_4 (.clk(in_1), .D(In_2[4]), .Q(out_7[0]), .en(En));  // open: Qn, preset, reset
  D_Flip_Flop d_ff_10 (.clk(in_1), .D(In_2[5]), .Q(out_7[1]), .en(En));  // open: Qn, preset, reset
  D_Flip_Flop d_ff_11 (.clk(in_1), .D(In_2[6]), .Q(out_7[2]), .en(En));  // open: Qn, preset, reset
  D_Flip_Flop d_ff_12 (.clk(in_1), .D(In_2[7]), .Q(out_7[3]), .en(En));  // open: Qn, preset, reset
  // Probe on out_5
  // Probe on out_6
  // Probe on out_7
  // Probe on out_8

  // Other names for the same wires on the sheet: CLK = in_1; WE = En
endmodule

module ALU (
  input  Carry_In,
  input  [7:0] A,
  input  [7:0] B,
  input  [3:0] Op,
  output [7:0] Result,
  output Carry_Out
);

  wire adder_1_cout, subtractor_1_bout, subtractor_2_bout;
  wire [7:0] adder_1_out, adder_2_out, and_1_out, not_1_out, or_1_out, shifter_1_out, shifter_2_out,
       subtractor_1_out, subtractor_2_out, subtractor_3_out, subtractor_4_out;

  Adder adder_1 (.a(A), .b(B), .out(adder_1_out), .cout(adder_1_cout));  // open: cin
  Subtractor subtractor_1 (.a(A), .b(B), .out(subtractor_1_out), .bout(subtractor_1_bout));  // open: bin
  Subtractor subtractor_2 (.a(B), .b(A), .out(subtractor_2_out), .bout(subtractor_2_bout));  // open: bin
  assign and_1_out = A & B;  // AND_Gate and_1, 8 bits wide
  assign or_1_out = A | B;  // OR_Gate or_1, 8 bits wide
  assign not_1_out = ~B;  // NOT_Gate not_1, 8 bits wide
  Adder adder_2 (.a(A), .b(B), .out(adder_2_out), .cin(Carry_In));  // open: cout
  Subtractor subtractor_3 (.a(A), .b(B), .out(subtractor_3_out), .bin(Carry_In));  // open: bout
  Subtractor subtractor_4 (.a(B), .b(A), .out(subtractor_4_out), .bin(Carry_In));  // open: bout
  Shifter shifter_1 (.in(A), .\dist (B[2:0]), .out(shifter_1_out));
  Shifter #(.shift("lr")) shifter_2 (.in(A), .\dist (B[2:0]), .out(shifter_2_out));
  Multiplexer #(.select(4), .width(8)) multiplexer_1 (
    .in0(adder_1_out), .in1(adder_1_out), .in2(subtractor_1_out), .in3(subtractor_2_out), .in4(and_1_out),
    .in5(or_1_out), .in6(not_1_out), .in7(shifter_1_out), .in8(shifter_2_out), .in9(adder_1_out),
    .in10(subtractor_1_out), .in11(shifter_1_out), .in12(shifter_2_out), .in13(adder_2_out),
    .in14(subtractor_3_out), .in15(subtractor_4_out), .out(Result), .sel(Op));  // open: en
  Multiplexer #(.select(4)) multiplexer_2 (
    .in0(1'b0), .in1(adder_1_cout), .in2(subtractor_1_bout), .in3(subtractor_2_bout), .in4(1'b0), .in5(1'b0),
    .in6(1'b0), .in7(1'b0), .in8(1'b0), .in9(1'b0), .in10(1'b0), .in11(1'b0), .in12(1'b0), .in13(1'b0),
    .in14(1'b0), .in15(1'b0), .out(Carry_Out), .sel(Op));  // open: en
endmodule

module register (
  input  [7:0] data,
  input  WE,
  input  [2:0] rs,
  input  [2:0] rd,
  input  in_5,
  output [7:0] rd_out,
  output [7:0] rs_out
);

  wire demultiplexer_1_out1, demultiplexer_1_out2, demultiplexer_1_out3, demultiplexer_1_out4,
       demultiplexer_1_out5, demultiplexer_1_out6, demultiplexer_1_out7;
  wire [7:0] r1_2_q, r1_3_q, r1_q, r2_2_q, r2_q, r3_2_q, r3_q;

  Demultiplexer #(.select(3)) demultiplexer_1 (
    .out1(demultiplexer_1_out1), .out2(demultiplexer_1_out2), .out3(demultiplexer_1_out3),
    .out4(demultiplexer_1_out4), .out5(demultiplexer_1_out5), .out6(demultiplexer_1_out6),
    .out7(demultiplexer_1_out7), .in(WE), .sel(rd));  // open: out0, en
  Register r1 (.D(data), .en(demultiplexer_1_out1), .Q(r1_q), .clk(in_5));  // open: clr
  Register r2 (.D(data), .en(demultiplexer_1_out2), .Q(r2_q), .clk(in_5));  // open: clr
  Register r3 (.D(data), .en(demultiplexer_1_out3), .Q(r3_q), .clk(in_5));  // open: clr
  Register r1_2 (.D(data), .en(demultiplexer_1_out4), .Q(r1_2_q), .clk(in_5));  // open: clr
  Register r2_2 (.D(data), .en(demultiplexer_1_out5), .Q(r2_2_q), .clk(in_5));  // open: clr
  Register r3_2 (.D(data), .en(demultiplexer_1_out6), .Q(r3_2_q), .clk(in_5));  // open: clr
  Register r1_3 (.D(data), .en(demultiplexer_1_out7), .Q(r1_3_q), .clk(in_5));  // open: clr
  Multiplexer #(.select(3), .width(8)) multiplexer_1 (
    .in0({8{1'b0}}), .in1(r1_q), .in2(r2_q), .in3(r3_q), .in4(r1_2_q), .in5(r2_2_q), .in6(r3_2_q),
    .in7(r1_3_q), .out(rd_out), .sel(rd));  // open: en
  // Probe on rd_out
  Multiplexer #(.select(3), .width(8)) multiplexer_2 (
    .in0({8{1'b0}}), .in1(r1_q), .in2(r2_q), .in3(r3_q), .in4(r1_2_q), .in5(r2_2_q), .in6(r3_2_q),
    .in7(r1_3_q), .out(rs_out), .sel(rs));  // open: en
  // Probe on rs_out

  // Other names for the same wires on the sheet: CLK = in_5
endmodule

// pc
module pc_control (
  input  [2:0] pc_op,
  input  clk,
  input  [7:0] imm,
  input  halt,
  input  [7:0] reg_rd,
  output [7:0] pc_out
);

  wire comparator_1_eq, comparator_1_gt, comparator_1_lt, not_1_p2, not_2_p2;
  wire [7:0] adder_1_out, multiplexer_1_out, multiplexer_2_out, multiplexer_3_out, multiplexer_4_out,
       multiplexer_5_out;

  Comparator comparator_1 (.a(reg_rd), .b({8{1'b0}}), .gt(comparator_1_gt), .eq(comparator_1_eq), .lt(comparator_1_lt));
  Multiplexer #(.width(8)) multiplexer_1 (
    .in0(adder_1_out), .in1(imm), .out(multiplexer_1_out), .sel(comparator_1_gt));  // open: en
  // NOT_Gate not_1: pin names not known; wires that end beside it: comparator_1_eq, not_1_p2
  Multiplexer #(.width(8)) multiplexer_2 (
    .in0(adder_1_out), .in1(imm), .out(multiplexer_2_out), .sel(comparator_1_lt));  // open: en
  Multiplexer #(.width(8)) multiplexer_3 (
    .in0(adder_1_out), .in1(imm), .out(multiplexer_3_out), .sel(not_1_p2));  // open: en
  Multiplexer #(.width(8)) multiplexer_4 (
    .in0(adder_1_out), .in1(imm), .out(multiplexer_4_out), .sel(comparator_1_eq));  // open: en
  Multiplexer #(.select(3), .width(8)) multiplexer_5 (
    .in0(adder_1_out), .in1(imm), .in2(reg_rd), .in3(imm), .in4(multiplexer_1_out), .in5(multiplexer_2_out),
    .in6(multiplexer_3_out), .in7(multiplexer_4_out), .out(multiplexer_5_out), .sel(pc_op));  // open: en
  // NOT_Gate not_2: pin names not known; wires that end beside it: halt, not_2_p2
  Register pc (.D(multiplexer_5_out), .en(not_2_p2), .Q(pc_out), .clk(clk));  // open: clr
  Adder adder_1 (.a(pc_out), .b(8'h1), .out(adder_1_out));  // open: cin, cout
endmodule

module control (
  input  [15:0] Instruction,
  output [7:0] imm,
  output memwe,
  output [2:0] rs,
  output [2:0] rd,
  output [1:0] reg_src,
  output HALT,
  output put,
  output li,
  output ld,
  output st,
  output j,
  output jal,
  output pc_we,
  output [3:0] ALUOp,
  output [2:0] PC_op,
  output alu_src,
  output rs_we,
  output reg_we
);

  wire adc, add, adi, \and , bez, bgz, blz, bnz, imm_we, jr, \not , not_1_out, \or , or_1_out, or_2_out, rsb,
       rsc, sbc, sbi, shl, shr, sli, sri, sub;

  // Decoder #(.select(5)) decoder_1: pin names not known; wires that end beside it: Instruction[15:11], HALT, put, li, ld, st, add, sub, rsb, \and , \or , \not , shl, shr, adi, sbi, sli, sri, adc, sbc, rsc, j, jr, jal, bgz, blz, bnz, bez
  Multiplexer #(.width(8)) multiplexer_1 (
    .in0({8{1'b0}}), .in1(Instruction[7:0]), .out(imm), .sel(imm_we));  // open: en
  or or_1 (or_1_out, adi, sbi);
  or or_2 (or_2_out, sli, sri);
  Priority_Encoder priority_encoder_1 (
    .in1(j), .in2(jr), .in3(jal), .in4(bgz), .in5(blz), .in6(bnz), .in7(bez), .gs(pc_we));  // open: in0, out, en_in, en_out
  Priority_Encoder priority_encoder_2 (
    .in0(1'b1), .in1(j), .in2(jr), .in3(jal), .in4(bgz), .in5(blz), .in6(bnz), .in7(bez), .out(PC_op));  // open: en_in, gs, en_out
  Priority_Encoder #(.select(4)) priority_encoder_3 (
    .in0(put), .in1(ld), .in2(st), .in3(add), .in4(sub), .in5(rsb), .in6(\and ), .in7(\or ), .in8(\not ),
    .in9(shl), .in10(shr), .in11(adc), .in12(sbc), .in13(rsc), .in14(1'b0), .in15(1'b0), .gs(rs_we));  // open: out, en_out, en_in
  and and_1 (reg_we, 1'b1, not_1_out);
  // NOT_Gate not_1 has open pins: in=open, out=not_1_out
  Priority_Encoder #(.select(4)) priority_encoder_4 (
    .in0(li), .in1(adi), .in2(sbi), .in3(sli), .in4(sri), .in5(j), .in6(jr), .in7(jal), .in8(bgz), .in9(blz),
    .in10(bnz), .in11(bez), .gs(imm_we));  // open: in12, in13, in14, in15, out, en_out, en_in
  // OR_Gate or_3: pin names not known; wires that end beside it: or_1_out, or_2_out, alu_src
  Priority_Encoder #(.select(4)) priority_encoder_5 (
    .in0(1'b1), .in1(add), .in2(sub), .in3(rsb), .in4(\and ), .in5(\or ), .in6(\not ), .in7(shl), .in8(shr),
    .in9(adi), .in10(sbi), .in11(sli), .in12(sri), .in13(adc), .in14(sbc), .in15(rsc), .out(ALUOp));  // open: gs, en_out, en_in
  Priority_Encoder #(.select(2)) priority_encoder_6 (
    .in0(1'b1), .in1(ld), .in2(li), .in3(jal), .out(reg_src));  // open: gs, en_out, en_in
  buf or_4 (memwe, st);  // OR_Gate

  assign rd = Instruction[10:8];
  assign rs = Instruction[2:0];

  // Other names for the same wires on the sheet: opcode[4:0] = Instruction[15:11]
endmodule
